// Digital circuit regfile.dig as structural Verilog
module regfile (
  input  [4:0] ReadReg1,
  input  [4:0] ReadReg2,
  input  [4:0] WriteReg,
  input  [31:0] WriteData,
  input  RegWrite,
  input  Clock,
  output [31:0] ReadData1,
  output [31:0] ReadData2
);

  RegisterFile #(.AddrBits(5), .Bits(32)) registerfile_1 (
    .Din(WriteData), .we(RegWrite), .Rw(WriteReg), .C(Clock), .Ra(ReadReg1), .Rb(ReadReg2), .Da(ReadData1),
    .Db(ReadData2));

  // Other names for the same wires on the sheet: rd1[31:0] = ReadData1; rd2[31:0] = ReadData2
endmodule

/* Test case regfile test:
ReadReg1 ReadReg2 WriteReg WriteData RegWrite Clock ReadData1 ReadData2
0 0 1 0x11 1 C 0x0 0x0
1 0 2 0x22 1 C 0x11 0x0
2 1 3 0x33 1 C 0x22 0x11
3 2 0 0x0 0 C 0x33 0x22
1 3 2 0x2222 1 C 0x11 0x33
2 2 4 0x44 0 C 0x2222 0x2222
2 3 4 0x44 1 C 0x2222 0x33
4 1 1 0x1111 1 C 0x44 0x1111
1 4 0 0x0 0 C 0x1111 0x44
*/
