// Digital circuit writeback_swapped.dig as structural Verilog
module writeback_swapped (
  input  Clock,
  input  [31:0] MemData,
  input  [31:0] ALUData,
  input  ResultSrc,
  input  [4:0] Rd,
  input  [4:0] Rs1,
  input  [4:0] Rs2,
  input  RegWrite,
  output [31:0] ReadData1,
  output [31:0] ReadData2
);

  wire [31:0] WriteBack;

  Multiplexer #(.Selector_Bits(1), .Bits(32)) multiplexer_1 (
    .sel(ResultSrc), .in_0(MemData), .in_1(ALUData), .out(WriteBack));
  regfile regfile_1 (
    .ReadReg1(Rs1), .ReadReg2(Rs2), .WriteReg(Rd), .WriteData(WriteBack), .RegWrite(RegWrite), .Clock(Clock),
    .ReadData1(ReadData1), .ReadData2(ReadData2));

  // Other names for the same wires on the sheet: clk = Clock; rd1[31:0] = ReadData1; rd2[31:0] = ReadData2
endmodule

/* Test case write-back:
MemData ALUData ResultSrc Rd Rs1 Rs2 RegWrite Clock ReadData1 ReadData2
0x51000001 0xA1000001 0 1 0 0 1 C 0x0 0x0
0xB2000002 0x62000002 1 2 0 0 1 C 0x0 0x0
0x53000003 0xA3000003 0 3 1 2 1 C 0xA1000001 0xB2000002
0x0 0x0 0 0 3 1 0 C 0xA3000003 0xA1000001
0xB4000004 0x64000004 1 4 2 3 1 C 0xB2000002 0xA3000003
0x0 0x0 0 0 4 2 0 C 0xB4000004 0xB2000002
0x55000005 0xA5000005 0 1 4 3 1 C 0xB4000004 0xA3000003
0x0 0x0 0 0 1 4 0 C 0xA5000005 0xB4000004
0xB6000006 0x66000006 1 5 1 2 1 C 0xA5000005 0xB2000002
0x0 0x0 0 0 5 3 0 C 0xB6000006 0xA3000003
0x77000007 0x77000007 0 6 0 0 1 C 0x0 0x0
0x0 0x0 0 0 6 0 0 C 0x77000007 0x0
0x88000008 0x88000008 1 7 6 0 1 C 0x77000007 0x0
0x0 0x0 0 0 7 6 0 C 0x88000008 0x77000007
0x0 0x0 0 0 0 7 0 C 0x0 0x88000008
0x0 0x0 0 0 5 7 0 C 0xB6000006 0x88000008
*/
