// Digital circuit two_wrong_gates.dig as structural Verilog
module two_wrong_gates (
  input  a,
  input  b,
  input  c,
  input  d,
  output Out1,
  output Out2
);

  or or_1 (Out1, a, b);
  and and_1 (Out2, c, d);

  // Other names for the same wires on the sheet: o1 = Out1; o2 = Out2
endmodule

/* Test case two gates:
a b c d Out1 Out2
0 0 0 0 0 0
0 1 0 0 0 0
1 1 0 0 1 0
0 0 0 1 0 1
1 1 1 0 1 1
1 0 0 0 0 0
0 0 1 1 0 0
*/
