// Digital circuit silent_detector.dig as structural Verilog
module silent_detector (
  input  [2:0] op,
  output W,
  output X,
  output Y,
  output Z
);

  wire hit, is_a, is_b, is_c, is_d, nop0, nop1, nop2;
  wire [1:0] addr;
  wire [3:0] cw_raw, hit4;

  not not_1 (nop0, op[0]);
  not not_2 (nop1, op[1]);
  not not_3 (nop2, op[2]);
  and u_is_a (is_a, op[0], nop1, nop2);
  and u_is_b (is_b, nop0, op[1], nop2);
  and u_is_c (is_c, op[0], op[1], op[2]);
  and u_is_d (is_d, nop0, nop1, op[2]);
  PriorityEncoder #(.Selector_Bits(2)) priorityencoder_1 (
    .in0(is_a), .in1(is_b), .in2(is_c), .in3(is_d), .num(addr), .any(hit));
  ROM #(.AddrBits(2), .Bits(4)) decode_ROM (.A(addr), .sel(1'b1), .D(cw_raw));
  BitExtender #(.inputBits(1), .outputBits(4)) bitextender_1 (.in(hit), .out(hit4));
  assign {Z, Y, X, W} = cw_raw & hit4;  // And and_1, 4 bits wide

  // Other names for the same wires on the sheet: cw[3:0] = {Z, Y, X, W}

  // Notes on the sheet:
  //   contents of decode_ROM (hex, n*v repeats v):
  //   9,6,a,5
endmodule

/* Test case decode:
op W X Y Z
0 0 0 0 0
1 1 0 0 1
2 0 1 1 0
3 0 1 0 1
4 1 0 1 0
5 0 0 0 0
6 0 0 0 0
7 0 0 0 0
*/
