// Digital circuit mini_alu_swapped_gate.dig as structural Verilog
module mini_alu_swapped_gate (
  input  [7:0] A,
  input  [7:0] B,
  input  [1:0] Op,
  output [7:0] Result
);

  wire isADD, isAND, isOR, isXOR;
  wire [1:0] S;
  wire [7:0] andO, orO, sumO, xorO;

  Add #(.Bits(8)) add_1 (.a(A), .b(B), .c_i(1'b0), .s(sumO));  // open: c_o
  assign xorO = A ^ B;  // XOr xor_1, 8 bits wide
  assign andO = A & B;  // And and_1, 8 bits wide
  assign orO = A | B;  // Or or_1, 8 bits wide
  Comparator #(.Bits(2)) comparator_1 (.a(Op), .b(2'b00), .eq(isAND));  // open: gt, lt
  Comparator #(.Bits(2)) comparator_2 (.a(Op), .b(2'b01), .eq(isOR));  // open: gt, lt
  Comparator #(.Bits(2)) comparator_3 (.a(Op), .b(2'b10), .eq(isADD));  // open: gt, lt
  Comparator #(.Bits(2)) comparator_4 (.a(Op), .b(2'b11), .eq(isXOR));  // open: gt, lt
  Multiplexer #(.Selector_Bits(2), .Bits(8)) multiplexer_1 (
    .sel(S), .in_0(andO), .in_1(orO), .in_2(sumO), .in_3(xorO), .out(Result));
  and and_2 (S[1], isADD, isXOR);
  or or_2 (S[0], isOR, isXOR);

  // Other names for the same wires on the sheet: res[7:0] = Result
endmodule

/* Test case mini alu:
A B Op Result
0xED 0xBF 0 0xAD
0x88 0x46 0 0x00
0x5F 0x03 0 0x03
0xAD 0xED 0 0xAD
0x29 0xAB 1 0xAB
0x14 0xC2 1 0xD6
0x56 0xE7 1 0xF7
0xD8 0x50 1 0xD8
0x56 0x79 2 0xCF
0x1A 0x38 2 0x52
0x43 0x20 2 0x63
0xC4 0x34 2 0xF8
0x95 0x68 3 0xFD
0x72 0xD7 3 0xA5
0x2C 0x88 3 0xA4
0x6B 0xCB 3 0xA0
*/
